# Fritzing sketch Robot Arm Schematic (saved by Fritzing 0.9.4)
breadboards: 2

parts:
  U1 = ESP32-38PinWide [part_number=ESP32-38PinWide]
  Power_plug1 = Power plug
  J9 = Basic Servo
  PWM1 = PCA9685 16x12-bit PWM Breakout
  J10 = Basic Servo
  J11 = Basic Servo
  J12 = Basic Servo
  J13 = Basic Servo
  J14 = Basic Servo

nets:
  GND: U1.GND, Power_plug1.GND, PWM1.no_name_yet#601, PWM1.no_name_yet#701, PWM1.no_name_yet#1000, PWM1.no_name_yet#1001, PWM1.no_name_yet#1002, PWM1.no_name_yet#1003, PWM1.no_name_yet#1004, PWM1.no_name_yet#1008
  N1: U1.VIN, PWM1.no_name_yet#605
  N2: U1.GPIO21, PWM1.no_name_yet#604
  N3: U1.GPIO22, PWM1.no_name_yet#603
  N4: Power_plug1.VCC, PWM1.no_name_yet#100, PWM1.no_name_yet#101, PWM1.no_name_yet#102, PWM1.no_name_yet#103, PWM1.no_name_yet#104, PWM1.no_name_yet#108, PWM1.no_name_yet#706
  N5: J9.pulse, PWM1.no_name_yet#0
  N6: PWM1.no_name_yet#1, J10.pulse
  N7: PWM1.no_name_yet#2, J11.pulse
  N8: PWM1.no_name_yet#3, J12.pulse
  N9: PWM1.no_name_yet#4, J13.pulse
  N10: PWM1.no_name_yet#8, J14.pulse

custom parts:
  ESP32-38PinWide: Generic 38-Pin ESP32 with wide format (only access to one side of pins on a breadboard) based on Stephen Lilley's HiLetgo ESP-WROOM-32 ESP32 ESP-32S Development Board.
